// Logisim project MpMp25.circ as structural Verilog: 6 circuits, main circuit main
module main (
  input  RST
);

  wire ALU_AccuEn, ALU_CE, ALU_F_E, and_2_out, and_3_out, and_4_out, CLK, CLK_E, clock_1_out, cu_1_clk_qtr,
       cu_1_io_input, cu_1_lng_jmp, cu_1_rf_ce0, cu_1_rf_ce1, cu_1_rf_data_out_0_e, cu_1_rf_pt_e,
       cu_1_rf_w_nr, decoder_1_out0, decoder_1_out1, decoder_1_out2, decoder_1_out3, decoder_1_out4,
       decoder_1_out5, decoder_2_out0, decoder_2_out1, decoder_2_out2, decoder_2_out3, decoder_2_out4,
       decoder_2_out5, decoder_2_out6, decoder_3_out0, decoder_3_out1, decoder_3_out7, or_1_out, PC_OVF,
       RAM_CE, RAM_WE, switch_1_p1;
  wire [0:0] keyboard_1_avail;
  wire [2:0] cu_1_reg0, cu_1_reg1;
  wire [3:0] ALU_CMD, joystick_1_x, joystick_1_y;
  wire [6:0] cu_1_const, keyboard_1_data;
  wire [7:0] Addr, alu_1_flag_out, alu_1_result, ALU_F_IN, DBG_LED, IO_8_B_q, IO_9_G_q, IO_a_R_q, IO_D_X_q,
       IO_F_Y_q, MEM_PAGE, PC, pull_resistor_2_node, ram_1_dout, register_2_q, rf_1_data_out0;
  wire [7:7] cu_1_const_2;
  wire [15:0] register_1_q, rom_1_data;

  Clock clock_1 (.out(clock_1_out));
  and and_1 (CLK, ~CLK_E, clock_1_out);  // AND_Gate
  CU cu_1 (
    .CLK(CLK), .RST(RST), .Instruction(rom_1_data), .ALU_F_IN(ALU_F_IN), .Reg0(cu_1_reg0), .Reg1(cu_1_reg1),
    .\const ({cu_1_const_2[7], cu_1_const}), .RF_W_nR(cu_1_rf_w_nr), .RF_CE0(cu_1_rf_ce0),
    .RF_CE1(cu_1_rf_ce1), .ALU_AccuEn(ALU_AccuEn), .ALU_CE(ALU_CE), .RAM_WE(RAM_WE), .RAM_CE(RAM_CE),
    .ALU_CMD(ALU_CMD), .RF_PT_E(cu_1_rf_pt_e), .CLK_QTR(cu_1_clk_qtr),
    .RF_Data_Out_0_E(cu_1_rf_data_out_0_e), .IO_Input(cu_1_io_input), .ADDR(Addr), .ALU_F_E(ALU_F_E),
    .LNG_JMP(cu_1_lng_jmp));  // open: RegResult
  assign {cu_1_const_2[7], cu_1_const} = cu_1_lng_jmp ? {{5{1'b0}}, cu_1_reg0} : 8'bz;  // Controlled_Buffer controlled_buffer_1
  assign Addr = cu_1_lng_jmp ? 8'hf9 : 8'bz;  // Controlled_Buffer controlled_buffer_2
  Register #(.width(16)) register_1 (.Q(register_1_q));  // open: D, en, clk, clr
  // Switch switch_1: pin names not known; wires that end beside it: switch_1_p1, CLK_E
  Comparator #(.width(16)) comparator_1 (.a(register_1_q), .b({MEM_PAGE, PC}), .eq(switch_1_p1));  // open: gt, lt
  RF rf_1 (
    .Addr0(cu_1_reg0), .Addr1(cu_1_reg1), .Data_In({cu_1_const_2[7], cu_1_const}), .W_nR(cu_1_rf_w_nr),
    .CE0(cu_1_rf_ce0), .CE1(cu_1_rf_ce1), .CLK(CLK), .RST(RST), .PTR_E(cu_1_rf_pt_e), .CLK_QTR(cu_1_clk_qtr),
    .Data_OUT0(rf_1_data_out0), .Data_OUT1({cu_1_const_2[7], cu_1_const}), .PC(PC), .PointerReg(Addr),
    .PC_OVF(PC_OVF));
  Hex_Digit_Display hex_digit_display_1 (.value(register_1_q[15:12]));  // open: dp
  Hex_Digit_Display hex_digit_display_2 (.value(register_1_q[11:8]));  // open: dp
  Pull_Resistor pull_resistor_1 (.node(CLK_E));
  Hex_Digit_Display hex_digit_display_3 (.value(MEM_PAGE[7:4]));  // open: dp
  Hex_Digit_Display hex_digit_display_4 (.value(register_1_q[7:4]));  // open: dp
  Hex_Digit_Display hex_digit_display_5 (.value(register_1_q[3:0]));  // open: dp
  Hex_Digit_Display hex_digit_display_6 (.value(MEM_PAGE[3:0]));  // open: dp
  Hex_Digit_Display hex_digit_display_7 (.value(PC[7:4]));  // open: dp
  ROM #(.addrWidth(16), .dataWidth(16)) rom_1 (.addr({MEM_PAGE, PC}), .data(rom_1_data));
  Hex_Digit_Display hex_digit_display_8 (.value(PC[3:0]));  // open: dp
  ALU alu_1 (
    .Flag_In(ALU_F_IN), .CMD_15_12(ALU_CMD), .Op0(rf_1_data_out0), .Op1({cu_1_const_2[7], cu_1_const}),
    .Result(alu_1_result), .Flag_Out(alu_1_flag_out));
  Decoder #(.select(3)) decoder_1 (
    .out0(decoder_1_out0), .out1(decoder_1_out1), .out2(decoder_1_out2), .out3(decoder_1_out3),
    .out4(decoder_1_out4), .out5(decoder_1_out5), .sel(Addr[2:0]), .en(and_2_out));  // open: out6, out7
  and and_2 (and_2_out, ~Addr[3], ~Addr[4], ~Addr[5], ~Addr[6], ~Addr[7], cu_1_io_input);  // AND_Gate
  and and_3 (and_3_out, Addr[3], ~Addr[4], ~Addr[5], ~Addr[6], ~Addr[7], cu_1_io_input);  // AND_Gate
  and and_4 (and_4_out, Addr[3], ~Addr[4], ~Addr[5], ~Addr[6], ~Addr[7], cu_1_io_input);  // AND_Gate
  // LedBar #(.inputtype("row")) ledbar_1: pin names not known; wires that end beside it: DBG_LED
  assign {cu_1_const_2[7], cu_1_const} = ALU_CE ? register_2_q : 8'bz;  // Controlled_Buffer controlled_buffer_3
  Register register_2 (.D(alu_1_result), .en(ALU_AccuEn), .Q(register_2_q), .clk(CLK), .clr(RST));
  Decoder #(.select(3)) decoder_2 (
    .out0(decoder_2_out0), .out1(decoder_2_out1), .out2(decoder_2_out2), .out3(decoder_2_out3),
    .out4(decoder_2_out4), .out5(decoder_2_out5), .out6(decoder_2_out6), .sel(Addr[2:0]), .en(and_3_out));  // open: out7
  Decoder #(.select(3)) decoder_3 (
    .out0(decoder_3_out0), .out1(decoder_3_out1), .out7(decoder_3_out7), .sel(Addr[2:0]), .en(and_4_out));  // open: out2, out3, out4, out5, out6
  assign {cu_1_const_2[7], cu_1_const} = cu_1_rf_data_out_0_e ? rf_1_data_out0 : 8'bz;  // Controlled_Buffer controlled_buffer_4
  Pull_Resistor pull_resistor_2 (.node(pull_resistor_2_node));
  assign pull_resistor_2_node = decoder_3_out7 ? {cu_1_const_2[7], cu_1_const} : 8'bz;  // Controlled_Buffer controlled_buffer_5
  RAM ram_1 (.addr(Addr), .we(RAM_WE), .oe(RAM_CE), .clk(CLK), .din({cu_1_const_2[7], cu_1_const}), .dout(ram_1_dout));
  TTY tty_1 (.data(cu_1_const), .clk(CLK), .we(decoder_1_out0), .clr(decoder_1_out1));
  Keyboard keyboard_1 (
    .clk(CLK), .re(decoder_1_out2), .clr(decoder_1_out4), .avail(keyboard_1_avail[0]), .data(keyboard_1_data));
  Register IO_8_B (.D({cu_1_const_2[7], cu_1_const}), .en(decoder_2_out0), .Q(IO_8_B_q), .clk(CLK), .clr(RST));
  Register IO_9_G (.D({cu_1_const_2[7], cu_1_const}), .en(decoder_2_out1), .Q(IO_9_G_q), .clk(CLK), .clr(RST));
  Register IO_a_R (.D({cu_1_const_2[7], cu_1_const}), .en(decoder_2_out2), .Q(IO_a_R_q), .clk(CLK), .clr(RST));
  Register IO_D_X (.D({cu_1_const_2[7], cu_1_const}), .en(decoder_2_out5), .Q(IO_D_X_q), .clk(CLK), .clr(RST));
  Register IO_F_Y (.D({cu_1_const_2[7], cu_1_const}), .en(decoder_2_out6), .Q(IO_F_Y_q), .clk(CLK), .clr(RST));
  Counter counter_1 (
    .load(decoder_3_out1), .D({cu_1_const_2[7], cu_1_const}), .count(PC_OVF), .Q(MEM_PAGE), .up(1'b1),
    .clk(CLK), .clr(RST));  // open: carry
  S_R_Flip_Flop s_r_ff_1 (.S(pull_resistor_2_node[0]), .clk(CLK), .R(RST), .Q(DBG_LED[0]));  // open: Qn, preset, reset
  S_R_Flip_Flop s_r_ff_2 (.S(pull_resistor_2_node[1]), .clk(CLK), .R(RST), .Q(DBG_LED[1]));  // open: Qn, preset, reset
  S_R_Flip_Flop s_r_ff_3 (.S(pull_resistor_2_node[2]), .clk(CLK), .R(RST), .Q(DBG_LED[2]));  // open: Qn, preset, reset
  S_R_Flip_Flop s_r_ff_4 (.S(pull_resistor_2_node[3]), .clk(CLK), .R(RST), .Q(DBG_LED[3]));  // open: Qn, preset, reset
  S_R_Flip_Flop s_r_ff_5 (.S(pull_resistor_2_node[4]), .clk(CLK), .R(RST), .Q(DBG_LED[4]));  // open: Qn, preset, reset
  S_R_Flip_Flop s_r_ff_6 (.S(pull_resistor_2_node[5]), .clk(CLK), .R(RST), .Q(DBG_LED[5]));  // open: Qn, preset, reset
  S_R_Flip_Flop s_r_ff_7 (.S(pull_resistor_2_node[6]), .clk(CLK), .R(RST), .Q(DBG_LED[6]));  // open: Qn, preset, reset
  S_R_Flip_Flop s_r_ff_8 (.S(pull_resistor_2_node[7]), .clk(CLK), .R(RST), .Q(DBG_LED[7]));  // open: Qn, preset, reset
  Register register_3 (.D(alu_1_flag_out), .en(ALU_F_E), .Q(ALU_F_IN), .clk(CLK), .clr(RST));
  assign {cu_1_const_2[7], cu_1_const} = decoder_3_out0 ? MEM_PAGE : 8'bz;  // Controlled_Buffer controlled_buffer_6
  or or_1 (or_1_out, RST, decoder_2_out3);
  assign {cu_1_const_2[7], cu_1_const} = RAM_CE ? ram_1_dout : 8'bz;  // Controlled_Buffer controlled_buffer_7
  assign {cu_1_const_2[7], cu_1_const} = decoder_1_out2 ? {1'b0, keyboard_1_data} : 8'bz;  // Controlled_Buffer controlled_buffer_8
  assign {cu_1_const_2[7], cu_1_const} = decoder_1_out3 ? {{7{1'b0}}, keyboard_1_avail[0]} : 8'bz;  // Controlled_Buffer controlled_buffer_9
  // RGB_Video #(.height(256), .width(256)) rgb_video_1: pin names not known; wires that end beside it: or_1_out, CLK, decoder_2_out4, IO_D_X_q, IO_F_Y_q, {IO_a_R_q, IO_9_G_q, IO_8_B_q}
  Joystick joystick_1 (.x(joystick_1_x), .y(joystick_1_y));
  assign {cu_1_const_2[7], cu_1_const} = decoder_1_out5 ? {joystick_1_y, joystick_1_x} : 8'bz;  // Controlled_Buffer controlled_buffer_10

  // Notes on the sheet:
  //   Instruction bus
  //   unused
  //   Data bus
  //   contents of rom_1 (hex, n*v repeats v):
  //   c013
  //   i/O Input
  //   Instruction BUS
  //   CE
  //   blank
  //   strope
  //   Page Registe I/O Addr. 9
  //   Paging Register
  //   256 Worte x 256 Seiten
  //   Pages: 0...FF, 100...1FF, ...
  //   in Hexanzeige von Program Memory dann 0100, wenn auf nächster Seite
  //   damit 65 kB RAM
  //   DATA BUS
endmodule

module ALU (
  input  [7:0] Op0,
  input  [7:0] Op1,
  input  [3:0] CMD_15_12,
  input  [7:0] Flag_In,
  output [7:0] Result,
  output [7:0] Flag_Out
);

  wire adder_1_cout, adder_2_cout, comparator_2_eq, multiplexer_1_out, multiplexer_3_out, multiplexer_4_out,
       R, shiftl_1_cout, subtractor_1_bout, subtractor_2_bout, xor_2_out, Z_out;
  wire [0:0] undriven;
  wire [7:0] adder_1_out, adder_2_out, and_1_out, divider_1_out, divider_1_rem, Flag_Select_data,
       multiplier_1_out, negator_1_out, not_1_out, or_1_out, shiftl_1_result, subtractor_1_out,
       subtractor_2_out, xnor_1_out, xor_1_out;
  wire [9:0] shifter_1_out;

  Adder adder_1 (.a(Op0), .b(Op1), .out(adder_1_out), .cout(adder_1_cout));  // open: cin
  Subtractor subtractor_1 (.a(Op1), .b(Op0), .out(subtractor_1_out), .bout(subtractor_1_bout));  // open: bin
  Multiplier multiplier_1 (.a(Op0), .b(Op1), .out(multiplier_1_out));  // open: cin, cout
  Divider divider_1 (.a(Op1), .b(Op0), .out(divider_1_out), .upper({8{1'b0}}), .rem(divider_1_rem));
  Negator negator_1 (.in(Op1), .out(negator_1_out));
  assign and_1_out = Op1 & Op0;  // AND_Gate and_1, 8 bits wide
  assign or_1_out = Op1 | Op0;  // OR_Gate or_1, 8 bits wide
  assign xor_1_out = Op1 ^ Op0;  // XOR_Gate xor_1, 8 bits wide
  assign xnor_1_out = ~(Op0 ^ Op1);  // XNOR_Gate xnor_1, 8 bits wide
  assign not_1_out = ~Op1;  // NOT_Gate not_1, 8 bits wide
  Adder adder_2 (.a(Op1), .b(Op0), .out(adder_2_out), .cin(Flag_In[1]), .cout(adder_2_cout));
  Subtractor subtractor_2 (.a(Op1), .b(Op0), .out(subtractor_2_out), .bin(Flag_In[1]), .bout(subtractor_2_bout));
  ROM #(.addrWidth(4)) Flag_Select (.addr(CMD_15_12), .data(Flag_Select_data));
  Comparator comparator_1 (.a({8{1'b0}}), .b(divider_1_rem), .gt(R));  // open: eq, lt
  ShiftL shiftl_1 (.Op(Op1), .Dist(Op0), .CIn(Flag_In[1]), .Result(shiftl_1_result), .COut(shiftl_1_cout));
  Shifter #(.shift("lr"), .width(10)) shifter_1 (
    .in({Flag_In[1], Op1, undriven[0]}), .\dist (Op0[3:0]), .out(shifter_1_out));
  Comparator comparator_2 (.a(Op0), .b({8{1'b0}}), .eq(comparator_2_eq));  // open: gt, lt
  Multiplexer #(.select(4)) multiplexer_1 (
    .in0(Flag_In[3]), .in1(Flag_In[3]), .in2(Flag_In[3]), .in3(comparator_2_eq), .in4(Flag_In[3]),
    .in5(Flag_In[3]), .in6(Flag_In[3]), .in7(Flag_In[3]), .in8(Flag_In[3]), .in9(Flag_In[3]),
    .in10(Flag_In[3]), .in11(Flag_In[3]), .in12(Flag_In[3]), .in13(Flag_In[3]), .in14(Flag_In[3]),
    .in15(Flag_In[3]), .out(multiplexer_1_out), .sel(CMD_15_12));
  xor xor_2 (xor_2_out, Result[7], Op1[7]);
  Multiplexer #(.select(4), .width(8)) multiplexer_2 (
    .in0(adder_1_out), .in1(subtractor_1_out), .in2(multiplier_1_out), .in3(divider_1_out),
    .in4(shiftl_1_result), .in5(shifter_1_out[8:1]), .in6(negator_1_out), .in7({8{1'b0}}), .in8({8{1'b0}}),
    .in9(and_1_out), .in10(or_1_out), .in11(xor_1_out), .in12(xnor_1_out), .in13(not_1_out),
    .in14(adder_2_out), .in15(subtractor_2_out), .out(Result), .sel(CMD_15_12));
  Multiplexer #(.select(4)) multiplexer_3 (
    .in0(adder_1_cout), .in1(subtractor_1_bout), .in2(Flag_In[1]), .in3(Flag_In[1]), .in4(shiftl_1_cout),
    .in5(shifter_1_out[9]), .in6(Flag_In[1]), .in7(Flag_In[1]), .in8(Flag_In[1]), .in9(Flag_In[1]),
    .in10(Flag_In[1]), .in11(Flag_In[1]), .in12(Flag_In[1]), .in13(Flag_In[1]), .in14(adder_2_cout),
    .in15(subtractor_2_bout), .out(multiplexer_3_out), .sel(CMD_15_12));
  Multiplexer #(.select(4)) multiplexer_4 (
    .in0(xor_2_out), .in1(xor_2_out), .in2(xor_2_out), .in3(Flag_In[2]), .in4(Flag_In[2]), .in5(Flag_In[2]),
    .in6(Flag_In[2]), .in7(Flag_In[2]), .in8(Flag_In[2]), .in9(Flag_In[2]), .in10(Flag_In[2]),
    .in11(Flag_In[2]), .in12(Flag_In[2]), .in13(Flag_In[2]), .in14(xor_2_out), .in15(xor_2_out),
    .out(multiplexer_4_out), .sel(CMD_15_12));
  // Probe on Result
  Multiplexer multiplexer_5 (.in0(Flag_In[0]), .in1(Z_out), .out(Flag_Out[0]), .sel(Flag_Select_data[0]));
  Multiplexer multiplexer_6 (.in0(Flag_In[1]), .in1(multiplexer_3_out), .out(Flag_Out[1]), .sel(Flag_Select_data[1]));
  Multiplexer multiplexer_7 (.in0(Flag_In[2]), .in1(multiplexer_4_out), .out(Flag_Out[2]), .sel(Flag_Select_data[2]));
  Multiplexer multiplexer_8 (.in0(Flag_In[3]), .in1(multiplexer_1_out), .out(Flag_Out[3]), .sel(Flag_Select_data[3]));
  Multiplexer multiplexer_9 (.in0(Flag_In[4]), .in1(R), .out(Flag_Out[4]), .sel(Flag_Select_data[4]));
  nor Z (Z_out, Result[0], Result[1], Result[2], Result[3], Result[4], Result[5], Result[6], Result[7]);

  assign Flag_Out[7:5] = Flag_In[7:5];

  // Other names for the same wires on the sheet: Op1_Tunnel[7:0] = Op1; C = Flag_In[1]; Op0_Tunnel[7:0] = Op0

  // Notes on the sheet:
  //   ADD 0, SUB 1, ADDC 14; SUBC 15
  //   ADD 0x00, SUB 0x01, ADDC 0x0E; SUBC 0x0F
  //   Op0
  //   Op1
  //   Op1 kommt immer zuerst; guck in Git!
  //   contents of Flag_Select (hex, n*v repeats v):
  //   3 1 3 0 2 2 8*0 2
  //     XXX,overflow_O, carry_C, zero_Z
  //   C_Flag
  //   O_Flag
  //   Z_Flag
  //   C_Flag
  //   O_Flag
  //   E_Flag
  //   R_Flag
endmodule

module CU (
  input  CLK,
  input  RST,
  input  [15:0] Instruction,
  input  [7:0] ALU_F_IN,
  output [2:0] Reg0,
  output [2:0] Reg1,
  output [2:0] RegResult,
  output [7:0] \const ,
  output RF_W_nR,
  output RF_CE0,
  output RF_CE1,
  output ALU_AccuEn,
  output ALU_CE,
  output RAM_WE,
  output RAM_CE,
  output [3:0] ALU_CMD,
  output RF_PT_E,
  output CLK_QTR,
  output RF_Data_Out_0_E,
  output IO_Input,
  output [7:0] ADDR,
  output ALU_F_E,
  output LNG_JMP
);

  wire Cycle_Zero, multiplexer_1_out;
  wire [1:0] Cyclecounter_q, rom_1_data_3;
  wire [2:0] Reg0_t, Reg1_t, register_1_q, RegResult_t;
  wire [3:0] rom_1_data_2;
  wire [3:3] register_1_q_2;
  wire [6:4] and_2_out;
  wire [7:0] mc_const8, multiplexer_2_out;
  wire [9:9] xor_1_out;
  wire [11:6] IR_q;
  wire [23:7] rom_1_data;

  Counter #(.max('h3), .width(2)) Cyclecounter (
    .Q(Cyclecounter_q), .carry(CLK_QTR), .clk(CLK), .clr(RST));  // open: load, D, count, up
  Register #(.width(16)) IR (
    .D(Instruction), .en(Cycle_Zero), .Q({ALU_CMD, IR_q[11], RegResult_t, IR_q[7:6], Reg1_t, Reg0_t}),
    .clk(CLK), .clr(RST));
  Multiplexer #(.select(3)) multiplexer_1 (
    .in0(1'b0), .in1(ALU_F_IN[0]), .in2(ALU_F_IN[1]), .in3(ALU_F_IN[2]), .in4(ALU_F_IN[3]),
    .in5(ALU_F_IN[4]), .in6(ALU_F_IN[5]), .in7(ALU_F_IN[6]), .out(multiplexer_1_out), .sel(register_1_q));
  and and_1 (and_2_out[6], IR_q[7], ~IR_q[11]);  // AND_Gate
  and and_2 (and_2_out[4], ~IR_q[11], IR_q[6]);  // AND_Gate
  nor nor_1 (Cycle_Zero, Cyclecounter_q[0], Cyclecounter_q[1]);
  Multiplexer #(.width(8)) multiplexer_2 (
    .in0({{5{1'b0}}, Reg0_t}), .in1({IR_q[7:6], Reg1_t, Reg0_t}), .out(multiplexer_2_out), .sel(IR_q[11]));
  xor xor_1 (xor_1_out[9], multiplexer_1_out, register_1_q_2[3]);
  ROM #(.addrWidth(10), .dataWidth(32)) rom_1 (
    .addr({xor_1_out[9], and_2_out[6], IR_q[11], and_2_out[4], ALU_CMD, Cyclecounter_q}),
    .data({mc_const8, rom_1_data[23:20], LNG_JMP, rom_1_data_2, ALU_F_E, rom_1_data[13], IO_Input, RF_Data_Out_0_E, rom_1_data_3[1], RF_PT_E, rom_1_data_3[0], rom_1_data[7], RAM_CE, RAM_WE, ALU_CE, ALU_AccuEn, RF_CE1, RF_CE0, RF_W_nR}));
  assign \const  = rom_1_data[7] ? multiplexer_2_out : 8'bz;  // Controlled_Buffer controlled_buffer_1
  Multiplexer #(.select(2), .width(3)) multiplexer_3 (
    .in0(RegResult_t), .in1(Reg0_t), .in2(Reg1_t), .out(Reg0), .sel(rom_1_data_3));  // open: in3
  assign ADDR = rom_1_data[13] ? multiplexer_2_out : 8'bz;  // Controlled_Buffer controlled_buffer_2
  assign ADDR = rom_1_data[20] ? mc_const8 : 8'bz;  // Controlled_Buffer controlled_buffer_3
  Register #(.width(4)) register_1 (
    .D(rom_1_data_2), .Q({register_1_q_2[3], register_1_q}), .clk(CLK), .clr(RST));  // open: en
  Multiplexer #(.width(3)) multiplexer_4 (.in0(Reg1_t), .in1(RegResult_t), .out(Reg1), .sel(rom_1_data_3[1]));

  // Notes on the sheet:
  //   IR
  //   Instruction Register
  //   IMOPb[7]
  //   IMOPa[11]
  //   CMD[6]
  //   CMD_const_8
  //   CMD0[15...12]
  //   2-0 Op0
  //   5-3 Op1
  //   10-8 RegR
  //   contents of rom_1 (hex, n*v repeats v):
  //   0 0 0 5 15*0 241 15*0 e22 13*0 9101004 902 15*0 10e 11 0 0 10e 11 0 0 10e 11 0 0 10e 11 0 0 10e 11 0
  //   0 10e 11 0 0 10e 11 10*0 10e 11 0 0 10e 11 0 0 10e 11 0 0 10e 11 0 0 10e 11 0 0 10e 11 0 0 10e 11
  //   34*0 81000 581 0 0 8000 0 0 0 10000 0 0 0 8000 81 0 0 10000 81 0 0 0 3004 0 0 0 3002 0 0 0 81 487*0
  //   81 0 0 0 81
  //   const_en
  //   Reg_ResOn0
  //   Reg_SLC
  //   Flag_Select_0
  //   Flag_Select_1
  //   Flag_Select_2
  //   Flag_neg
  //   mc_const8_E
  //   Addr_E
endmodule

module RF (
  input  [2:0] Addr0,
  input  [2:0] Addr1,
  input  [7:0] Data_In,
  input  W_nR,
  input  CE0,
  input  CE1,
  input  CLK,
  input  RST,
  input  PTR_E,
  input  CLK_QTR,
  output [7:0] Data_OUT0,
  output [7:0] Data_OUT1,
  output [7:0] PC,
  output [7:0] PointerReg,
  output PC_OVF
);

  wire and_1_out, and_2_out, decoder_1_out1, decoder_1_out2, decoder_1_out3, decoder_1_out4, decoder_1_out5,
       decoder_1_out6, decoder_1_out7, PC_OVF_t, PC_SLC;
  wire [7:0] register_1_q, register_2_q, register_3_q, register_4_q, register_5_q, register_6_q,
       Stack_Pointer_q;

  Decoder #(.select(3)) decoder_1 (
    .out0(PC_SLC), .out1(decoder_1_out1), .out2(decoder_1_out2), .out3(decoder_1_out3),
    .out4(decoder_1_out4), .out5(decoder_1_out5), .out6(decoder_1_out6), .out7(decoder_1_out7), .sel(Addr0),
    .en(W_nR));
  and and_1 (and_1_out, ~Addr0[0], ~Addr0[1], ~Addr0[2], W_nR);  // AND_Gate
  and and_2 (and_2_out, CLK_QTR, ~and_1_out);  // AND_Gate
  Counter #(.trigger("falling")) counter_1 (
    .load(PC_SLC), .D(Data_In), .count(and_2_out), .Q(PC), .carry(PC_OVF_t), .up(1'b1), .clk(CLK), .clr(RST));
  Register Stack_Pointer (.D(Data_In), .en(decoder_1_out1), .Q(Stack_Pointer_q), .clk(CLK), .clr(RST));
  Register register_1 (.D(Data_In), .en(decoder_1_out2), .Q(register_1_q), .clk(CLK), .clr(RST));
  Register register_2 (.D(Data_In), .en(decoder_1_out3), .Q(register_2_q), .clk(CLK), .clr(RST));
  Register register_3 (.D(Data_In), .en(decoder_1_out4), .Q(register_3_q), .clk(CLK), .clr(RST));
  Register register_4 (.D(Data_In), .en(decoder_1_out5), .Q(register_4_q), .clk(CLK), .clr(RST));
  Register register_5 (.D(Data_In), .en(decoder_1_out6), .Q(register_5_q), .clk(CLK), .clr(RST));
  Register register_6 (.D(Data_In), .en(decoder_1_out7), .Q(register_6_q), .clk(CLK), .clr(RST));
  Multiplexer #(.disabled("Z"), .enable("true"), .select(3), .width(8)) multiplexer_1 (
    .in0(PC), .in1(Stack_Pointer_q), .in2(register_1_q), .in3(register_2_q), .in4(register_3_q),
    .in5(register_4_q), .in6(register_5_q), .in7(register_6_q), .out(Data_OUT0), .sel(Addr0), .en(CE0));
  Multiplexer #(.disabled("Z"), .enable("true"), .select(3), .width(8)) multiplexer_2 (
    .in0(PC), .in1(Stack_Pointer_q), .in2(register_1_q), .in3(register_2_q), .in4(register_3_q),
    .in5(register_4_q), .in6(register_5_q), .in7(register_6_q), .out(Data_OUT1), .sel(Addr1), .en(CE1));
  Multiplexer #(.disabled("Z"), .enable("true"), .select(3), .width(8)) multiplexer_3 (
    .in0(PC), .in1(Stack_Pointer_q), .in2(register_1_q), .in3(register_2_q), .in4(register_3_q),
    .in5(register_4_q), .in6(register_5_q), .in7(register_6_q), .out(PointerReg), .sel(Addr1), .en(PTR_E));
  and and_3 (PC_OVF, PC_OVF_t, CLK_QTR, ~PC_SLC);  // AND_Gate

  // Notes on the sheet:
  //   Registerfile
  //   Speicherdecoder wann geschrieben wird
  //   Read notWrite
  //   Chipenable
  //   speicher in dem register sind 
  //   1
  //   6
  //   Pc
  //   2
  //   3
  //   4
  //   5
  //   7
endmodule

module test_ALU (
);

  wire and_1_out, and_2_out, clock_1_out, comparator_1_eq, comparator_2_eq;
  wire [3:0] ALU_Command_data;
  wire [7:0] alu_1_flag_out, alu_1_result, Flag_result_data, Flags_In_data, Op0_data, Op1_data, Result_data;
  wire [9:0] Adresse;

  Clock clock_1 (.out(clock_1_out));
  Hex_Digit_Display hex_digit_display_1 (.value({2'b00, Adresse[9:8]}));  // open: dp
  Hex_Digit_Display hex_digit_display_2 (.value(Adresse[7:4]));  // open: dp
  and and_1 (and_1_out, clock_1_out, and_2_out);
  Hex_Digit_Display hex_digit_display_3 (.value(Adresse[3:0]));  // open: dp
  Counter #(.max('h3ff), .trigger("falling"), .width(10)) counter_1 (
    .Q(Adresse), .clk(and_1_out));  // open: load, D, count, carry, up, clr
  ROM #(.addrWidth(10), .dataWidth(4)) ALU_Command (.addr(Adresse), .data(ALU_Command_data));
  ROM #(.addrWidth(10)) Op0 (.addr(Adresse), .data(Op0_data));
  ROM #(.addrWidth(10)) Op1 (.addr(Adresse), .data(Op1_data));
  ROM #(.addrWidth(10)) Result (.addr(Adresse), .data(Result_data));
  ALU alu_1 (
    .Flag_In(Flags_In_data), .Op0(Op0_data), .Op1(Op1_data), .Result(alu_1_result), .Flag_Out(alu_1_flag_out));  // open: CMD_15_12
  Comparator comparator_1 (.a(alu_1_result), .b(Result_data), .eq(comparator_1_eq));  // open: gt, lt
  ROM #(.addrWidth(10)) Flags_In (.addr(Adresse), .data(Flags_In_data));
  ROM #(.addrWidth(10)) Flag_result (.addr(Adresse), .data(Flag_result_data));
  Comparator comparator_2 (.a(Flag_result_data), .b(alu_1_flag_out), .eq(comparator_2_eq));  // open: gt, lt
  LED led_1 (.in(and_2_out));
  and and_2 (and_2_out, comparator_2_eq, comparator_1_eq);

  // Notes on the sheet:
  //   contents of Op0 (hex, n*v repeats v):
  //   1 2 3 aa ff
  //   contents of Op1 (hex, n*v repeats v):
  //   4 5 6 57 1
  //   contents of Result (hex, n*v repeats v):
  //   5 7 9 1
  //   CMD15_12
  //   Op1
  //   Result
  //   Op0
  //   Flag_In
  //   Flag_Out
  //   contents of Flag_result (hex, n*v repeats v):
  //   0 0 0 2 3
endmodule

module ShiftL (
  input  [7:0] Op,
  input  [7:0] Dist,
  input  CIn,
  output [7:0] Result,
  output COut
);

  wire comparator_1_eq;
  wire [3:0] subtractor_1_out;
  wire [8:0] shifter_1_out;

  Shifter #(.width(9)) shifter_1 (.in({Op, CIn}), .\dist (subtractor_1_out), .out(shifter_1_out));
  Subtractor #(.width(4)) subtractor_1 (.a(Dist[3:0]), .b(4'b0001), .out(subtractor_1_out));  // open: bin, bout
  Comparator comparator_1 (.a(Dist), .b({8{1'b0}}), .eq(comparator_1_eq));  // open: gt, lt
  Multiplexer #(.width(9)) multiplexer_1 (
    .in0(shifter_1_out), .in1({1'b0, Op}), .out({COut, Result}), .sel(comparator_1_eq));
endmodule
